# Fritzing sketch ratpack_wifly (saved by Fritzing 0.7.10b)
breadboards: 1

parts:
  S1 = Pushbutton [package=THT]
  R1 = Resistor [tolerance=±5% resistance=10k package=THT]
  Arduino_Uno = Arduino
  Wifly_Shield = Arduino WiFly Shield
  R2 = Resistor [tolerance=±5% resistance=220 package=THT]
  LED1 = LED - 5mm [color="Green (555nm)" package="5 mm [THT]"]

nets:
  +5V: S1.leg0, Arduino_Uno.+5V, Wifly_Shield.5V
  N1: S1.leg1, R1.Pin_1, Arduino_Uno.D2, Wifly_Shield.D2
  GND: R1.Pin_0, Arduino_Uno.GND, Wifly_Shield.GND, LED1.cathode
  N2: Arduino_Uno.D9, Wifly_Shield.D9, R2.Pin_0
  N3: R2.Pin_1, LED1.anode

notes:
  makingthingshappen.de
  Rat Pack
